# Fritzing sketch DesktopLight (saved by Fritzing 0.9.3b)
breadboards: 1

parts:
  Part1 = Breadboard Power Supply Board SMD
  Q1 = PNP-Transistor [package="TO92 [THT]"]
  Q2 = PNP-Transistor [package="TO92 [THT]"]
  S1 = Toggle Switch [package=THT]
  Part2 = Arduino Uno (Rev3)
  R1 = Resistor [tolerance=±5% resistance=10k package=THT]
  R2 = Resistor [tolerance=±5% resistance=10k package=THT]
  R3 = Rotary Potentiometer (Small) [maximum_resistance=100kΩ package=THT]
  R4 = Rotary Potentiometer (Small) [maximum_resistance=100kΩ package=THT]
  LED2 = RGB LED (com. cathode, rgb) [package="5 mm [THT]"]
  LED3 = RGB LED (com. cathode, rgb) [package="5 mm [THT]"]
  R5 = Resistor [tolerance=±5% resistance=1k package=THT]
  R6 = Resistor [tolerance=±5% resistance=1k package=THT]
  R7 = Resistor [tolerance=±5% resistance=1k package=THT]
  R8 = Resistor [tolerance=±5% resistance=1k package=THT]
  R9 = Resistor [tolerance=±5% resistance=1k package=THT]
  R10 = Resistor [tolerance=±5% resistance=1k package=THT]

nets:
  N1: Part1.GND, S1.L1, LED2.common_cathode, LED3.common_cathode
  N2: Part1.VCC, S1.L2
  N3: Q1.E, Q2.E, S1.COM, R7.Pin_1, R8.Pin_1
  N4: Q1.B, R2.Pin_1
  N5: Q1.C, R5.Pin_1, R6.Pin_1
  N6: Q2.B, R1.Pin_1
  N7: Q2.C, R9.Pin_0, R10.Pin_0
  N8: Part2.A4/SDA, R4.wiper
  N9: Part2.A5/SCL, R3.wiper
  N10: Part2.D3_PWM, R1.Pin_0
  N11: Part2.D5_PWM, R2.Pin_0
  N12: Part2.5V, R3.leg1, R4.leg1
  N13: Part2.GND, R3.leg2, R4.leg2
  N14: LED2.red_anode, R9.Pin_1
  N15: LED2.green_anode, R7.Pin_0
  N16: LED2.blue_anode, R5.Pin_0
  N17: LED3.red_anode, R10.Pin_1
  N18: LED3.green_anode, R8.Pin_0
  N19: LED3.blue_anode, R6.Pin_0
